# Fritzing sketch Stepper Motor and TB6612 (saved by Fritzing 1.0.7)
breadboards: 1

parts:
  Part1 = Arduino Nano (Rev3.0) (ICSP)
  Part2 = Adafruit TB6612 DC and Stepper Motor Driver [part_number="Adafruit #2448"]
  M1 = Stepper Motor - Bipolar
  JACK1 = 2.1mm Barrel Jack with Terminal Block

nets:
  GND: Part1.GND, Part2.GND, JACK1.NEG
  N1: Part1.D4, Part2.AIN2
  N2: Part1.D5, Part2.AIN1
  N3: Part1.D6, Part2.BIN1
  N4: Part1.D7, Part2.BIN2
  5V: Part1.5V, Part2.VCC, Part2.PWMB, Part2.STBY, Part2.PWMA
  N5: Part2.PWRIN, JACK1.POS
  N6: Part2.MOTORA1, M1.D
  N7: Part2.MOTORA2, M1.B
  N8: Part2.MOTORB2, M1.C
  N9: Part2.MOTORB1, M1.A
