# Fritzing sketch Stepper Motor and TB6612 (saved by Fritzing 1.0.7)
breadboards: 1

parts:
  Part1 = Arduino Nano (Rev3.0) (ICSP)
  Part2 = Adafruit TB6612 DC and Stepper Motor Driver [part_number="Adafruit #2448"]
  M1 = Stepper Motor - Bipolar
  JACK1 = 2.1mm Barrel Jack with Terminal Block
  Part3 = InvenSense MPU6050
  Mod1 = KY-003 Hall Magnetic Sensor Module [package="Breakout board"]

nets:
  GND: Part1.GND, Part2.GND, JACK1.NEG, Part3.GND, Mod1.-
  N1: Part1.D2, Mod1.S
  N2: Part1.D4, Part2.AIN2
  N3: Part1.D5, Part2.AIN1
  N4: Part1.D6, Part2.BIN1
  N5: Part1.D7, Part2.BIN2
  VCC: Part1.5V, Part2.VCC, Part2.PWMB, Part2.STBY, Part2.PWMA, Part3.VCC, Mod1.Vin
  N6: Part1.A6, Part3.SDA
  N7: Part1.A5, Part3.SCL
  N8: Part2.PWRIN, JACK1.POS
  N9: Part2.MOTORA1, Part2.MOTORA2, Part2.MOTORB2, M1.C, M1.B, M1.D
  N10: Part2.MOTORB1, M1.A

custom parts:
  KY-003 Hall Magnetic Sensor Module: KEYES KY-003 Arduino Hall Magnetic Sensor Module is a switch that will turn on/off in the presence of a magnetic field.
